# Fritzing sketch servo-joystick (saved by Fritzing 0.9.3b)
breadboards: 1

parts:
  Part1 = Arduino Uno (Rev3)
  J1 = Basic Servo  # not connected
  Part2 = Thumb Joystick

nets:
  N1: Part1.A0, Part2.HORZ
  N2: Part1.A1, Part2.VERT
  N3: Part1.D4, Part2.VCC
  N4: Part1.5V, Part2.SEL
  GND: Part1.GND, Part2.GND
